// Logisim project seq_circuit.circ as structural Verilog: 1 circuit, main circuit main
module main (
  input  x,
  input  y
);

  wire and_1_out, and_2_out, or_1_out, undriven, xor_1_out, xor_2_out;

  ExactlyOne xor_1 (.out(xor_1_out), .in0(x), .in1(x), .in3(y), .in4(y));
  and and_1 (and_1_out, x, y);
  xor xor_2 (xor_2_out, xor_1_out, undriven);
  and and_2 (and_2_out, xor_1_out, undriven);
  D_Flip_Flop d_ff_1 (.clk(undriven));  // open: D, Q, Qn, preset, en, reset
  or or_1 (or_1_out, and_2_out, and_1_out);

  // Notes on the sheet:
  //   S
  //   C
endmodule
